// Logisim project alu-1bit.circ as structural Verilog
module ALU_1_bit (
  input  A,
  input  B,
  input  [2:0] in_3,
  input  Less,
  input  Cin,
  input  Sub,
  output \Saída ,
  output Set,
  output Cout
);

  wire and_1_out, nor_1_out, or_1_out, xor_1_out, xor_2_out;

  and and_1 (and_1_out, A, B);
  or or_1 (or_1_out, A, B);
  xor xor_1 (xor_1_out, A, B);
  nor nor_1 (nor_1_out, A, B);
  xor xor_2 (xor_2_out, B, Sub);
  Adder #(.width(1)) adder_1 (.a(A), .b(xor_2_out), .out(Set), .cin(Cin), .cout(Cout));
  Multiplexer #(.select(3), .enable("false")) multiplexer_1 (
    .in0(and_1_out), .in1(or_1_out), .in2(xor_1_out), .in3(nor_1_out), .in4(Set), .in5(Less), .out(\Saída ),
    .sel(in_3));  // open: in6, in7
endmodule
