// Logisim project alu.circ as structural Verilog
module ALU_1_bit (
  input  A,
  input  B,
  input  [2:0] in_3,
  input  Less,
  input  Cin,
  input  Sub,
  output \Saída ,
  output Set,
  output Cout
);

  wire and_1_out, nor_1_out, or_1_out, xor_1_out, xor_2_out;

  and and_1 (and_1_out, A, B);
  or or_1 (or_1_out, A, B);
  xor xor_1 (xor_1_out, A, B);
  nor nor_1 (nor_1_out, A, B);
  xor xor_2 (xor_2_out, B, Sub);
  Adder #(.width(1)) adder_1 (.a(A), .b(xor_2_out), .out(Set), .cin(Cin), .cout(Cout));
  Multiplexer #(.select(3), .enable("false")) multiplexer_1 (
    .in0(and_1_out), .in1(or_1_out), .in2(xor_1_out), .in3(nor_1_out), .in4(Set), .in5(Less), .out(\Saída ),
    .sel(in_3));  // open: in6, in7
endmodule

module ALU (
  input  in_1,
  input  Sub,
  input  [2:0] Op,
  input  [7:0] A,
  input  [7:0] B,
  output [7:0] S
);

  wire alu_1_bit_1_cout, alu_1_bit_2_cout, alu_1_bit_3_cout, alu_1_bit_4_cout, alu_1_bit_5_cout,
       alu_1_bit_6_cout, alu_1_bit_7_cout, alu_1_bit_8_set;

  ALU_1_bit alu_1_bit_1 (
    .A(A[0]), .B(B[0]), .Less(alu_1_bit_8_set), .Cin(Sub), .Sub(Sub), .\Saída (S[0]),
    .Cout(alu_1_bit_1_cout), .in_3(Op));  // open: Set
  ALU_1_bit alu_1_bit_2 (
    .A(A[1]), .B(B[1]), .Less(in_1), .Cin(alu_1_bit_1_cout), .Sub(Sub), .\Saída (S[1]),
    .Cout(alu_1_bit_2_cout), .in_3(Op));  // open: Set
  ALU_1_bit alu_1_bit_3 (
    .A(A[2]), .B(B[2]), .Less(in_1), .Cin(alu_1_bit_2_cout), .Sub(Sub), .\Saída (S[2]),
    .Cout(alu_1_bit_3_cout), .in_3(Op));  // open: Set
  ALU_1_bit alu_1_bit_4 (
    .A(A[3]), .B(B[3]), .Less(in_1), .Cin(alu_1_bit_3_cout), .Sub(Sub), .\Saída (S[3]),
    .Cout(alu_1_bit_4_cout), .in_3(Op));  // open: Set
  ALU_1_bit alu_1_bit_5 (
    .A(A[4]), .B(B[4]), .Less(in_1), .Cin(alu_1_bit_4_cout), .Sub(Sub), .\Saída (S[4]),
    .Cout(alu_1_bit_5_cout), .in_3(Op));  // open: Set
  ALU_1_bit alu_1_bit_6 (
    .A(A[5]), .B(B[5]), .Less(in_1), .Cin(alu_1_bit_5_cout), .Sub(Sub), .\Saída (S[5]),
    .Cout(alu_1_bit_6_cout), .in_3(Op));  // open: Set
  ALU_1_bit alu_1_bit_7 (
    .A(A[6]), .B(B[6]), .Less(in_1), .Cin(alu_1_bit_6_cout), .Sub(Sub), .\Saída (S[6]),
    .Cout(alu_1_bit_7_cout), .in_3(Op));  // open: Set
  ALU_1_bit alu_1_bit_8 (
    .A(A[7]), .B(B[7]), .Less(in_1), .Cin(alu_1_bit_7_cout), .Sub(Sub), .\Saída (S[7]),
    .Set(alu_1_bit_8_set), .in_3(Op));  // open: Cout
endmodule
