// Logisim project somador-1bit.circ as structural Verilog
module Somador (
  input  A,
  input  B,
  input  C,
  output Carry,
  output Soma
);

  wire and_1_out, and_2_out, and_3_out;

  and and_1 (and_1_out, A, B);
  and and_2 (and_2_out, A, C);
  and and_3 (and_3_out, B, C);
  xor xor_1 (Soma, A, B, C);
  or or_1 (Carry, and_1_out, and_2_out, and_3_out);
endmodule
