// Logisim project somador-4bit.circ as structural Verilog: 2 circuits, main circuit Somador
module main (
  input  [3:0] A,
  input  in_2,
  input  in_3,
  input  in_4,
  input  in_5,
  output out_6,
  output out_7,
  output out_8,
  output out_9,
  output out_10
);

  wire somador_2_carry, somador_3_carry, somador_4_carry;

  Somador somador_1 (.A(A[3]), .B(in_2), .C(somador_2_carry), .Soma(out_7), .Carry(out_6));
  Somador somador_2 (.A(A[2]), .B(in_3), .C(somador_3_carry), .Soma(out_8), .Carry(somador_2_carry));
  Somador somador_3 (.A(A[1]), .B(in_4), .C(somador_4_carry), .Soma(out_9), .Carry(somador_3_carry));
  Somador somador_4 (.A(A[0]), .B(in_5), .C(1'b0), .Soma(out_10), .Carry(somador_4_carry));
endmodule

module Somador (
  input  A,
  input  B,
  input  C,
  output Carry,
  output Soma
);

  wire and_1_out, and_2_out, and_3_out;

  and and_1 (and_1_out, A, B);
  and and_2 (and_2_out, A, C);
  and and_3 (and_3_out, B, C);
  xor xor_1 (Soma, A, B, C);
  or or_1 (Carry, and_1_out, and_2_out, and_3_out);
endmodule
